// Logisim project 10bitInputOr.circ as structural Verilog: 2 circuits, main circuit main
module main (
  input  in_1,
  input  in_2,
  input  in_3,
  input  in_4,
  input  in_5,
  input  in_6,
  input  in_7,
  input  in_8,
  input  in_9,
  input  in_10,
  output out_11
);

  _10InputOr u_10inputor_1 (
    .in_1(in_1), .in_2(in_2), .in_3(in_3), .in_4(in_4), .in_5(in_5), .in_6(in_6), .in_7(in_7), .in_8(in_8),
    .in_9(in_9), .in_10(in_10), .out_11(out_11));
endmodule

module _10InputOr (
  input  in_1,
  input  in_2,
  input  in_3,
  input  in_4,
  input  in_5,
  input  in_6,
  input  in_7,
  input  in_8,
  input  in_9,
  input  in_10,
  output out_11
);

  wire n7425_1_p5, n7425_2_p5, n7432_1_p3, n7432_1_p4, n7432_1_p5, n7432_1_p6;

  // _7425 7425_1: pin names not known; wires that end beside it: in_1, in_2, in_3, in_4, n7425_1_p5
  // _7425 7425_2: pin names not known; wires that end beside it: in_5, in_6, in_7, in_8, n7425_2_p5
  // _7432 7432_1: pin names not known; wires that end beside it: in_9, in_10, n7432_1_p3, n7432_1_p4, n7432_1_p5, n7432_1_p6, n7432_1_p6, n7432_1_p3, out_11
  // _7404 7404_1: pin names not known; wires that end beside it: n7425_1_p5, n7432_1_p4, n7425_2_p5, n7432_1_p5
endmodule
