// Logisim project AdderLib.circ as structural Verilog: 9 circuits, main circuit 4Adder
// 4Add
module _4Adder (
  input  [3:0] A,
  input  [3:0] B,
  input  Cin,
  output [3:0] S,
  output Cout
);

  // _7483 7483_1: pin names not known; wires that end beside it: A[3], S[2], A[2], B[2], 1'b1, S[1], B[1], A[1], B[3], S[3], Cout, Cin, 1'b0, B[0], A[0], S[0]
endmodule

// 32Add
module _32Adder (
  input  [31:0] A,
  input  [31:0] B,
  input  Cin,
  output [31:0] S,
  output Cout
);

  wire n4adder_1_cout, n4adder_2_cout, n4adder_3_cout, n4adder_4_cout, n4adder_5_cout, n4adder_6_cout,
       n4adder_7_cout;

  _4Adder u_4adder_1 (.A(A[3:0]), .B(B[3:0]), .Cin(Cin), .S(S[3:0]), .Cout(n4adder_1_cout));
  _4Adder u_4adder_2 (.A(A[7:4]), .B(B[7:4]), .Cin(n4adder_1_cout), .S(S[7:4]), .Cout(n4adder_2_cout));
  _4Adder u_4adder_3 (.A(A[11:8]), .B(B[11:8]), .Cin(n4adder_2_cout), .S(S[11:8]), .Cout(n4adder_3_cout));
  _4Adder u_4adder_4 (.A(A[15:12]), .B(B[15:12]), .Cin(n4adder_3_cout), .S(S[15:12]), .Cout(n4adder_4_cout));
  _4Adder u_4adder_5 (.A(A[19:16]), .B(B[19:16]), .Cin(n4adder_4_cout), .S(S[19:16]), .Cout(n4adder_5_cout));
  _4Adder u_4adder_6 (.A(A[23:20]), .B(B[23:20]), .Cin(n4adder_5_cout), .S(S[23:20]), .Cout(n4adder_6_cout));
  _4Adder u_4adder_7 (.A(A[27:24]), .B(B[27:24]), .Cin(n4adder_6_cout), .S(S[27:24]), .Cout(n4adder_7_cout));
  _4Adder u_4adder_8 (.A(A[31:28]), .B(B[31:28]), .Cin(n4adder_7_cout), .S(S[31:28]), .Cout(Cout));
endmodule

// 12Add
module _11Adder (
  input  [10:0] A,
  input  [10:0] B,
  input  Cin,
  output [10:0] S,
  output Cout
);

  wire n4adder_1_cout, n4adder_2_cout;

  _4Adder u_4adder_1 (.A(A[3:0]), .B(B[3:0]), .Cin(Cin), .S(S[3:0]), .Cout(n4adder_1_cout));
  _4Adder u_4adder_2 (.A(A[7:4]), .B(B[7:4]), .Cin(n4adder_1_cout), .S(S[7:4]), .Cout(n4adder_2_cout));
  _4Adder u_4adder_3 (
    .A({1'b0, A[10:8]}), .B({1'b0, B[10:8]}), .Cin(n4adder_2_cout), .S({Cout, S[10:8]}));  // open: Cout
endmodule

// 1Cl4
module _1Compl4 (
  input  [3:0] A,
  output [3:0] O
);

  // _7486 7486_1: pin names not known; wires that end beside it: A[0], 1'b1, O[0], A[1], 1'b1, O[1], 1'b0, 1'b1, 1'b1, A[3], O[3], 1'b1, A[2], O[2]
endmodule

// 1Cl12
module _1Compl11 (
  input  [10:0] A,
  output [10:0] O
);

  wire [3:3] n1compl4_2_o;

  _1Compl4 u_1compl4_1 (.A(A[7:4]), .O(O[7:4]));
  _1Compl4 u_1compl4_2 (.A({1'b0, A[10:8]}), .O({n1compl4_2_o[3], O[10:8]}));
  _1Compl4 u_1compl4_3 (.A(A[3:0]), .O(O[3:0]));
endmodule

// 1Cl32
module _1Compl32 (
  input  [31:0] A,
  output [31:0] O
);

  _1Compl4 u_1compl4_1 (.A(A[3:0]), .O(O[3:0]));
  _1Compl4 u_1compl4_2 (.A(A[7:4]), .O(O[7:4]));
  _1Compl4 u_1compl4_3 (.A(A[11:8]), .O(O[11:8]));
  _1Compl4 u_1compl4_4 (.A(A[15:12]), .O(O[15:12]));
  _1Compl4 u_1compl4_5 (.A(A[19:16]), .O(O[19:16]));
  _1Compl4 u_1compl4_6 (.A(A[23:20]), .O(O[23:20]));
  _1Compl4 u_1compl4_7 (.A(A[27:24]), .O(O[27:24]));
  _1Compl4 u_1compl4_8 (.A(A[31:28]), .O(O[31:28]));
endmodule

// 2Cl12
module _2Compl11 (
  input  [10:0] A,
  output [10:0] O
);

  wire [10:0] n1compl11_1_o;

  _1Compl11 u_1compl11_1 (.A(A), .O(n1compl11_1_o));
  _11Adder u_11adder_1 (.A(n1compl11_1_o), .B({11{1'b0}}), .Cin(1'b1), .S(O));  // open: Cout
endmodule

// 2Cl32
module _2Compl32 (
  input  [31:0] A,
  output [31:0] O
);

  wire [31:0] n1compl32_1_o;

  _1Compl32 u_1compl32_1 (.A(A), .O(n1compl32_1_o));
  _32Adder u_32adder_1 (.A(n1compl32_1_o), .B({32{1'b0}}), .Cin(1'b1), .S(O));  // open: Cout
endmodule

// 12Sub
module _11Sub (
  input  [10:0] A,
  input  [10:0] B,
  output [10:0] A_B
);

  wire [10:0] n1compl11_1_o;

  _1Compl11 u_1compl11_1 (.A(B), .O(n1compl11_1_o));
  _11Adder u_11adder_1 (.A(A), .B(n1compl11_1_o), .Cin(1'b1), .S(A_B));  // open: Cout
endmodule
