// Logisim project ComparatorLib.circ as structural Verilog: 1 circuit, main circuit 11BitMagnitudeComparator
// 11Comp
module _11BitMagnitudeComparator (
  input  SA,
  input  SB,
  input  [10:0] A,
  input  [10:0] B,
  output Switch,
  output A_B
);

  wire ic_7485_1_p10, ic_7485_2_p12, ic_7485_2_p14, ic_7485_2_p15, ic_7485_2_p16, ic_7485_3_p12, n7486_1_p3,
       n7486_1_p8;

  // _7486 7486_1: pin names not known; wires that end beside it: SA, SB, n7486_1_p3, 1'b0, 1'b1, SB, A_B, n7486_1_p8
  // IC_7485 ic_7485_1: pin names not known; wires that end beside it: A[0], A[1], A[2], A[3], B[0], B[1], B[2], B[3], 1'b0, ic_7485_1_p10
  // IC_7485 ic_7485_2: pin names not known; wires that end beside it: 1'b1, 1'b0, A[4], A[5], A[6], A[7], B[4], B[5], B[6], B[7], ic_7485_1_p10, ic_7485_2_p12, ic_7485_2_p12, ic_7485_2_p14, ic_7485_2_p15, ic_7485_2_p16
  // IC_7485 ic_7485_3: pin names not known; wires that end beside it: ic_7485_2_p14, A[8], A[9], A[10], 1'b0, B[8], B[9], B[10], 1'b0, ic_7485_2_p15, ic_7485_2_p16, ic_7485_3_p12, ic_7485_3_p12, A_B
  // _7408 7408_1: pin names not known; wires that end beside it: n7486_1_p3, n7486_1_p8, Switch
endmodule
