// Logisim project FPA.circ as structural Verilog: 2 circuits, main circuit main
module main (
  input  [31:0] A,
  input  [31:0] B,
  output [31:0] Result,
  output out_4,
  output out_5
);

  FPA fpa_1 (.A(A), .B(B), .Result(Result), .out_4(out_4), .out_5(out_4));

  assign out_5 = out_4;
endmodule

module FPA (
  input  [31:0] A,
  input  [31:0] B,
  output [31:0] Result,
  output out_4,
  output out_5
);

  wire addedinp_1_a_b, addedinp_1_cout, addedinp_1_flag, addedinp_1_sa, addedinp_1_saxorsb, addedinp_1_sb,
       addedinp_1_sign_bit, inputcheck_1_flag, n7408_1_p5, normalization_1_valid, roundingmachine_1_exp_cin;
  wire [10:0] addedinp_1_exp_large, n11adder_1_s, normalization_1_add_with_exp;
  wire [19:0] n32to20_1_o;
  wire [31:0] addedinp_1_to_normalize, n0handler_1_o, n0handler_2_o, n32mux2x1_1_o, normalization_1_out,
       outputprocess_1_float, roundingmachine_1_o;

  _0handler u_0handler_1 (.A(A), .O(n0handler_1_o));
  _0handler u_0handler_2 (.A(B), .O(n0handler_2_o));
  InputCheck inputcheck_1 (.A(n0handler_1_o), .B(n0handler_2_o), .flag(inputcheck_1_flag));  // open: A0
  AddedInp addedinp_1 (
    .A(n0handler_1_o), .B(n0handler_2_o), .A_B(addedinp_1_a_b), .Flag(addedinp_1_flag), .SA(addedinp_1_sa),
    .SB(addedinp_1_sb), .to_normalize(addedinp_1_to_normalize), .Cout(addedinp_1_cout),
    .Sign_bit(addedinp_1_sign_bit), .Exp_Large(addedinp_1_exp_large), .SAxorSB(addedinp_1_saxorsb));
  Normalization normalization_1 (
    .SA(addedinp_1_sa), .SB(addedinp_1_sb), .I(addedinp_1_to_normalize), .Exp(addedinp_1_exp_large),
    .S1xorS2(addedinp_1_saxorsb), .Cout(addedinp_1_cout), .Valid(normalization_1_valid),
    .Out(normalization_1_out), .Add_with_exp(normalization_1_add_with_exp));
  // _7408 7408_1: pin names not known; wires that end beside it: addedinp_1_saxorsb, addedinp_1_cout, inputcheck_1_flag, addedinp_1_flag, n7408_1_p5, 1'b0, 1'b1
  RoundingMachine roundingmachine_1 (
    .A(normalization_1_out), .O(roundingmachine_1_o), .Exp_Cin(roundingmachine_1_exp_cin));
  _11Adder u_11adder_1 (
    .A(addedinp_1_exp_large), .B(normalization_1_add_with_exp), .Cin(roundingmachine_1_exp_cin),
    .S(n11adder_1_s));  // open: Cout
  _32to20 u_32to20_1 (.A(roundingmachine_1_o), .O(n32to20_1_o));
  OutputProcess outputprocess_1 (
    .Sign(addedinp_1_sign_bit), .Exp(n11adder_1_s), .Frac(n32to20_1_o), .Float(outputprocess_1_float));
  OverflowTest_main main_1 (
    .Exp(addedinp_1_exp_large), .Exp_2(normalization_1_add_with_exp), .Exp_3(11'h1), .in_4(1'b0),
    .in_5(1'b0), .out_6(out_4));
  Underflow_main main_2 (.Exp(addedinp_1_exp_large), .Add_with_exp(normalization_1_add_with_exp), .out_3(out_5));
  _32Mux4X1 u_32mux4x1_1 (
    .A(n0handler_2_o), .B(n0handler_1_o), .C(n32mux2x1_1_o), .D(n32mux2x1_1_o), .S1(n7408_1_p5),
    .S0(addedinp_1_a_b), .E_prime(1'b0), .O(Result));
  _32Mux2X1 u_32mux2x1_1 (
    .A({32{1'b0}}), .B(outputprocess_1_float), .E_prime(1'b0), .S(normalization_1_valid), .O(n32mux2x1_1_o));
endmodule
