// Logisim project InputHandler.circ as structural Verilog: 2 circuits, main circuit ExpDiff12
// ExpDiff
module ExpDiff12 (
  input  SA,
  input  SB,
  input  [10:0] A,
  input  [10:0] B,
  output Switch,
  output A_B,
  output [10:0] A_nB,
  output [10:0] Exp_Large
);

  wire [10:0] n11mux2x1_1_o;

  _11BitMagnitudeComparator u_11bitmagnitudecomparator_1 (.SA(SA), .SB(SB), .A(A), .B(B), .Switch(Switch), .A_B(A_B));
  _11Mux2X1 u_11mux2x1_1 (.A(A), .B(B), .E_prime(1'b0), .S(A_B), .O(n11mux2x1_1_o));
  _11Mux2X1 u_11mux2x1_2 (.A(B), .B(A), .E_prime(1'b0), .S(A_B), .O(Exp_Large));
  _11Sub u_11sub_1 (.A(Exp_Large), .B(n11mux2x1_1_o), .A_B(A_nB));
endmodule

// InpProc
module InputHandle (
  input  SA,
  input  SB,
  input  [31:0] Fraction1,
  input  [31:0] Fraction2,
  input  [10:0] A_Exp,
  input  [10:0] B_Exp,
  output Switch,
  output [31:0] Large,
  output [31:0] Small,
  output [10:0] ExpDiff,
  output [10:0] Exp_Large,
  output A_B
);

  ExpDiff12 expdiff12_1 (
    .SA(SA), .SB(SB), .A(A_Exp), .B(B_Exp), .Switch(Switch), .A_B(A_B), .A_nB(ExpDiff), .Exp_Large(Exp_Large));
  _32Mux2X1 u_32mux2x1_1 (.A(Fraction2), .B(Fraction1), .E_prime(1'b0), .S(A_B), .O(Large));
  _32Mux2X1 u_32mux2x1_2 (.A(Fraction1), .B(Fraction2), .E_prime(1'b0), .S(A_B), .O(Small));
endmodule
