// Logisim project MiscLib.circ as structural Verilog: 14 circuits, main circuit 20to32
// 20T32
module _20to32 (
  input  [19:0] in_1,
  output [31:0] out_2
);


  assign out_2 = {1'b1, in_1, {11{1'b0}}};
endmodule

// 19T32
module _19to32 (
  input  [18:0] in_1,
  output [31:0] out_2
);


  assign out_2 = {1'b1, in_1, {12{1'b0}}};
endmodule

// Rnd
module Rounding (
  input  [31:0] A,
  output O
);

  wire n7432_1_p3, n7432_1_p6, n7432_1_p11, n7432_1_p14, n7432_2_p3, n7432_2_p6, n7432_2_p11, n7432_2_p14,
       n7432_3_p3, n7432_3_p6, n7432_3_p11, n7432_3_p14;

  // _7432 7432_1: pin names not known; wires that end beside it: A[0], A[1], n7432_1_p3, n7432_1_p3, A[2], n7432_1_p6, 1'b0, 1'b1, n7432_1_p6, A[3], n7432_1_p11, n7432_1_p11, A[4], n7432_1_p14
  // _7432 7432_2: pin names not known; wires that end beside it: n7432_1_p14, A[5], n7432_2_p3, n7432_2_p3, A[6], n7432_2_p6, 1'b0, 1'b1, n7432_2_p6, A[7], n7432_2_p11, n7432_2_p11, A[8], n7432_2_p14
  // _7432 7432_3: pin names not known; wires that end beside it: n7432_2_p14, A[9], n7432_3_p3, n7432_3_p3, A[10], n7432_3_p6, 1'b0, 1'b1, n7432_3_p6, A[11], n7432_3_p11, n7432_3_p11, A[13], n7432_3_p14
  // _7408 7408_1: pin names not known; wires that end beside it: n7432_3_p14, A[12], O, 1'b0, 1'b1
endmodule

// 5T12
module _5to12 (
  input  [4:0] A,
  output [11:0] O
);


  assign O = {{7{1'b0}}, A};
endmodule

// 32T19
module _32to19 (
  input  [31:0] A,
  output [18:0] O
);


  assign O = A[31:13];
endmodule

// OP
module OutputProcess (
  input  Sign,
  input  [11:0] Exp,
  input  [18:0] Frac,
  output [31:0] Float
);


  assign Float = {Sign, Exp, Frac};
endmodule

// IP
module InputProcess (
  input  [31:0] in_1,
  output Sign,
  output [11:0] Exp,
  output [31:0] Frac
);

  wire n12is0_1_o;
  wire [31:0] n19to32_1_out_2;

  _19to32 u_19to32_1 (.in_1(in_1[18:0]), .out_2(n19to32_1_out_2));
  _12Is0 u_12is0_1 (.A(in_1[30:19]), .O(n12is0_1_o));
  // _7408 7408_1: pin names not known; wires that end beside it: in_1[31], n12is0_1_o, Sign, 1'b0, 1'b1
  _32Mux2X1 u_32mux2x1_1 (.A({32{1'b0}}), .B(n19to32_1_out_2), .E_prime(1'b0), .S(n12is0_1_o), .O(Frac));

  assign Exp = in_1[30:19];
endmodule

module _12Is0 (
  input  [11:0] A,
  output O
);

  wire n7432_1_p3, n7432_1_p6, n7432_1_p10, n7432_2_p2, n7432_2_p4, n7432_2_p7, n7432_2_p12, n7432_3_p2,
       n7432_3_p4, n7432_3_p7;

  // _7432 7432_1: pin names not known; wires that end beside it: A[0], A[1], n7432_1_p3, n7432_1_p3, A[2], n7432_1_p6, 1'b1, n7432_1_p6, A[3], n7432_1_p10, n7432_1_p10, A[4]
  // _7432 7432_2: pin names not known; wires that end beside it: 1'b0, n7432_2_p2, A[5], n7432_2_p4, n7432_2_p4, A[6], n7432_2_p7, n7432_2_p2, 1'b1, n7432_2_p7, A[7], n7432_2_p12, n7432_2_p12, A[8]
  // _7432 7432_3: pin names not known; wires that end beside it: 1'b0, n7432_3_p2, A[9], n7432_3_p4, n7432_3_p4, A[10], n7432_3_p7, 1'b0, n7432_3_p2, 1'b1, n7432_3_p7, A[11], O
endmodule

// InCheck
module InputCheck (
  input  [31:0] A,
  input  [31:0] B,
  output flag,
  output A0
);

  wire n12is0_2_o;

  _12Is0 u_12is0_1 (.A(A[30:19]), .O(A0));
  _12Is0 u_12is0_2 (.A(B[30:19]), .O(n12is0_2_o));
  // _7408 7408_1: pin names not known; wires that end beside it: A0, n12is0_2_o, flag, 1'b0, 1'b1
endmodule

module _4OR (
  input  [3:0] A,
  input  [3:0] B,
  output [3:0] out_3
);

  // _7432 7432_1: pin names not known; wires that end beside it: A[0], B[0], out_3[0], A[1], B[1], out_3[1], 1'b0, 1'b1, A[2], B[2], out_3[2], A[3], B[3], out_3[3]
endmodule

module _32OR (
  input  [31:0] A,
  input  [31:0] B,
  output [31:0] O
);

  _4OR u_4or_1 (.A(A[3:0]), .B(B[3:0]), .out_3(O[3:0]));
  _4OR u_4or_2 (.A(A[11:8]), .B(B[11:8]), .out_3(O[11:8]));
  _4OR u_4or_3 (.A(A[19:16]), .B(B[19:16]), .out_3(O[19:16]));
  _4OR u_4or_4 (.A(A[27:24]), .B(B[27:24]), .out_3(O[27:24]));
  _4OR u_4or_5 (.A(A[7:4]), .B(B[7:4]), .out_3(O[7:4]));
  _4OR u_4or_6 (.A(A[15:12]), .B(B[15:12]), .out_3(O[15:12]));
  _4OR u_4or_7 (.A(A[23:20]), .B(B[23:20]), .out_3(O[23:20]));
  _4OR u_4or_8 (.A(A[31:28]), .B(B[31:28]), .out_3(O[31:28]));
endmodule

// 0hand
module _0handler (
  input  [31:0] A,
  output [31:0] O
);

  wire n12is0_1_o;

  _12Is0 u_12is0_1 (.A(A[30:19]), .O(n12is0_1_o));
  // _7408 7408_1: pin names not known; wires that end beside it: n12is0_1_o, A[31], O[31], 1'b0, 1'b1

  assign O[30:0] = A[30:0];
endmodule

module _32Is0 (
  input  [31:0] A,
  output Flag
);

  wire n4is0_1_flag, n4is0_2_flag, n4is0_3_flag, n4is0_4_flag, n4is0_5_flag, n4is0_6_flag, n4is0_7_flag;

  _4Is0 u_4is0_1 (.A(A[3:0]), .Prev(1'b0), .Flag(n4is0_1_flag));
  _4Is0 u_4is0_2 (.A(A[7:4]), .Prev(n4is0_1_flag), .Flag(n4is0_2_flag));
  _4Is0 u_4is0_3 (.A(A[11:8]), .Prev(n4is0_2_flag), .Flag(n4is0_3_flag));
  _4Is0 u_4is0_4 (.A(A[15:12]), .Prev(n4is0_3_flag), .Flag(n4is0_4_flag));
  _4Is0 u_4is0_5 (.A(A[19:16]), .Prev(n4is0_4_flag), .Flag(n4is0_5_flag));
  _4Is0 u_4is0_6 (.A(A[23:20]), .Prev(n4is0_5_flag), .Flag(n4is0_6_flag));
  _4Is0 u_4is0_7 (.A(A[27:24]), .Prev(n4is0_6_flag), .Flag(n4is0_7_flag));
  _4Is0 u_4is0_8 (.A(A[31:28]), .Prev(n4is0_7_flag), .Flag(Flag));
endmodule

module _4Is0 (
  input  [3:0] A,
  input  Prev,
  output Flag
);

  wire n7432_1_p3, n7432_1_p6, n7432_1_p11;

  // _7432 7432_1: pin names not known; wires that end beside it: A[0], A[1], n7432_1_p3, n7432_1_p3, A[2], n7432_1_p6, 1'b0, 1'b1, n7432_1_p6, A[3], n7432_1_p11, n7432_1_p11, Prev, Flag
endmodule
