// Logisim project OverflowTest.circ as structural Verilog: 3 circuits, main circuit main
module main (
  input  [10:0] Exp,
  input  [10:0] Exp_2,
  input  [10:0] Exp_3,
  input  in_4,
  input  in_5,
  output out_6
);

  wire helper2_1_cout;
  wire [10:0] helper_1_s;

  helper helper_1 (.Exp(Exp), .Add_with_exp(Exp_2), .Cin(in_4), .S(helper_1_s));  // open: Cout
  helper2 helper2_1 (.Exp(helper_1_s), .Add_with_exp(Exp_3), .Cin(in_5), .Cout(helper2_1_cout));
  // IC_7408 ic_7408_1: pin names not known; wires that end beside it: Exp[10], helper2_1_cout, out_6
endmodule

module helper (
  input  [10:0] Exp,
  input  [10:0] Add_with_exp,
  input  Cin,
  output [10:0] S,
  output Cout
);

  wire n4adder_1_cout, n4adder_2_cout;

  _4Adder u_4adder_1 (.A(Exp[3:0]), .B(Add_with_exp[3:0]), .Cin(Cin), .S(S[3:0]), .Cout(n4adder_1_cout));
  _4Adder u_4adder_2 (.A(Exp[7:4]), .B(Add_with_exp[7:4]), .Cin(n4adder_1_cout), .S(S[7:4]), .Cout(n4adder_2_cout));
  _4Adder u_4adder_3 (
    .A({1'b0, Exp[10:8]}), .B({1'b0, Add_with_exp[10:8]}), .Cin(n4adder_2_cout), .S({Cout, S[10:8]}));  // open: Cout
endmodule

module helper2 (
  input  [10:0] Exp,
  input  [10:0] Add_with_exp,
  input  Cin,
  output Cout
);

  wire n4adder_1_cout, n4adder_2_cout;
  wire [2:0] n4adder_3_s;
  wire [3:0] n4adder_1_s, n4adder_2_s;

  _4Adder u_4adder_1 (.A(Exp[3:0]), .B(Add_with_exp[3:0]), .Cin(Cin), .S(n4adder_1_s), .Cout(n4adder_1_cout));
  _4Adder u_4adder_2 (
    .A(Exp[7:4]), .B(Add_with_exp[7:4]), .Cin(n4adder_1_cout), .S(n4adder_2_s), .Cout(n4adder_2_cout));
  _4Adder u_4adder_3 (
    .A({1'b0, Exp[10:8]}), .B({1'b0, Add_with_exp[10:8]}), .Cin(n4adder_2_cout), .S({Cout, n4adder_3_s}));  // open: Cout
endmodule
