// Logisim project Rounder.circ as structural Verilog
module Rounder (
  input  [31:0] A,
  output out_2
);

  wire n10inputor_1_out_11, n7432_1_p3, n7432_1_p6;

  _10InputOr u_10inputor_1 (
    .in_1(A[0]), .in_2(A[1]), .in_3(A[2]), .in_4(A[3]), .in_5(A[4]), .in_6(A[5]), .in_7(A[6]), .in_8(A[7]),
    .in_9(A[8]), .in_10(A[9]), .out_11(n10inputor_1_out_11));
  // _7432 7432_1: pin names not known; wires that end beside it: n10inputor_1_out_11, A[10], n7432_1_p3, n7432_1_p3, A[12], n7432_1_p6
  // _7408 7408_1: pin names not known; wires that end beside it: n7432_1_p6, A[11], out_2
endmodule
