// Logisim project RoundingMachine.circ as structural Verilog: 1 circuit, main circuit RoundingMachine
// RM
module RoundingMachine (
  input  [31:0] A,
  output [31:0] O,
  output Exp_Cin
);

  wire [12:12] rounder_1_out_2;

  Rounder rounder_1 (.A(A), .out_2(rounder_1_out_2[12]));
  _32Adder u_32adder_1 (.A({{19{1'b0}}, rounder_1_out_2[12], {12{1'b0}}}), .B(A), .Cin(1'b0), .S(O), .Cout(Exp_Cin));
endmodule
