// Logisim project Underflow.circ as structural Verilog: 2 circuits, main circuit main
module main (
  input  [10:0] Exp,
  input  [10:0] Add_with_exp,
  output out_3
);

  wire helper_1_out_4, ic_7404_1_p2;
  wire [10:0] n11adder_1_s;

  _11Adder u_11adder_1 (.A(11'h401), .B(Exp), .Cin(1'b0), .S(n11adder_1_s));  // open: Cout
  helper helper_1 (.A(n11adder_1_s), .B(Add_with_exp), .Cin(1'b0), .out_4(helper_1_out_4));
  // IC_7404 ic_7404_1: pin names not known; wires that end beside it: Exp[10], ic_7404_1_p2
  // IC_7408 ic_7408_1: pin names not known; wires that end beside it: ic_7404_1_p2, helper_1_out_4, out_3
endmodule

module helper (
  input  [10:0] A,
  input  [10:0] B,
  input  Cin,
  output out_4
);

  wire ic_7432_1_p1, ic_7432_1_p2, main_1_out_11, n4adder_1_cout, n4adder_2_cout;
  wire [3:0] n4adder_1_s, n4adder_2_s, n4adder_3_s;

  _4Adder u_4adder_1 (.A(A[3:0]), .B(B[3:0]), .Cin(Cin), .S(n4adder_1_s), .Cout(n4adder_1_cout));
  _4Adder u_4adder_2 (.A(A[7:4]), .B(B[7:4]), .Cin(n4adder_1_cout), .S(n4adder_2_s), .Cout(n4adder_2_cout));
  _4Adder u_4adder_3 (.A({1'b0, A[10:8]}), .B({1'b0, B[10:8]}), .Cin(n4adder_2_cout), .S(n4adder_3_s));  // open: Cout
  _10bitInputOr_main main_1 (
    .in_1(1'b0), .in_2(n4adder_1_s[1]), .in_3(n4adder_1_s[2]), .in_4(n4adder_1_s[3]), .in_5(n4adder_2_s[0]),
    .in_6(n4adder_2_s[1]), .in_7(n4adder_2_s[2]), .in_8(n4adder_2_s[3]), .in_9(n4adder_3_s[0]),
    .in_10(n4adder_3_s[1]), .out_11(main_1_out_11));
  // IC_7432 ic_7432_1: pin names not known; wires that end beside it: ic_7432_1_p1, ic_7432_1_p2, out_4
  // IC_7404 ic_7404_1: pin names not known; wires that end beside it: n4adder_3_s[2], main_1_out_11, ic_7432_1_p2, ic_7432_1_p1
endmodule
